# Fritzing sketch breadboard (saved by Fritzing 0.9.2b)
circuit board: 8.46667cm x 5.64444cm
breadboards: 1
stripboards: 1

parts:
  R1 = Resistor [tolerance=±5% resistance=100 package=THT]
  R2 = Resistor [tolerance=±5% resistance=100 package=THT]
  R3 = Resistor [tolerance=±5% resistance=100 package=THT]
  R4 = Resistor [tolerance=±5% resistance=100 package=THT]
  R5 = Resistor [tolerance=±5% resistance=100 package=THT]
  R6 = Resistor [tolerance=±5% resistance=100 package=THT]
  R7 = Resistor [tolerance=±5% resistance=100 package=THT]
  R8 = Resistor [tolerance=±5% resistance=100 package=THT]
  IC1 = IC, DIP package, 20 pins [chip_label=SN74HCT245N]
  JP2 = Header 3 [package=molex-1x3_lock]
  JP3 = Header 3 [package=molex-1x3_lock]
  JP4 = Header 3 [package=molex-1x3_lock]
  JP5 = Header 3 [package=molex-1x3_lock]
  JP6 = Header 3 [package=molex-1x3_lock]
  JP7 = Header 3 [package=molex-1x3_lock]
  JP8 = Header 3 [package=molex-1x3_lock]
  JP1 = Header 3 [package=molex-1x3_lock]
  Teensy1 = Teensy 3.0

nets:
  N1: R1.Pin_0, IC1.pin18
  N2: R1.Pin_1, JP1.2
  N3: R2.Pin_0, IC1.pin17
  N4: R2.Pin_1, JP2.2
  N5: R3.Pin_0, IC1.pin16
  N6: R3.Pin_1, JP3.2
  N7: R4.Pin_0, IC1.pin15
  N8: R4.Pin_1, JP4.2
  N9: R5.Pin_0, IC1.pin14
  N10: R5.Pin_1, JP5.2
  N11: R6.Pin_0, IC1.pin13
  N12: R6.Pin_1, JP6.2
  N13: R7.Pin_0, IC1.pin12
  N14: R7.Pin_1, JP7.2
  N15: R8.Pin_0, IC1.pin11
  N16: R8.Pin_1, JP8.2
  5V: IC1.pin1, IC1.pin20, JP2.1, JP3.1, JP4.1, JP5.1, JP6.1, JP7.1, JP8.1, JP1.1, Teensy1.Vin
  N17: IC1.pin2, Teensy1.D2
  strip 2: IC1.pin3, Teensy1.A0/D14
  N18: IC1.pin4, Teensy1.D7
  N19: IC1.pin5, Teensy1.D8
  N20: IC1.pin6, Teensy1.D6
  strip 6: IC1.pin7, Teensy1.A6/D20
  strip 7: IC1.pin8, Teensy1.A7/D21
  N21: IC1.pin9, Teensy1.D5
  GND: IC1.pin10, IC1.pin19, JP2.3, JP3.3, JP4.3, JP5.3, JP6.3, JP7.3, JP8.3, JP1.3, Teensy1.GND
  N22: Teensy1.A1/D15, Teensy1.A2/D16
